# Fritzing sketch BLE_Pulse_TMP36_Sketch (saved by Fritzing 0.9.3b)
breadboards: 1

parts:
  Part1 = Arduino Nano 33 IOT
  U1 = TMP36 [package=to-92]
  SEN1 = Pulse Sensor [package=SIP]
  LED1 = LEDs [package=led10mm]
  LED2 = smd LED [color="Red (633nm)" package="0603 [SMD]"]

nets:
  N1: Part1.RESET, Part1.A7
  GND: Part1.GND, Part1.D13~, U1.GND, SEN1.GND, LED1.C, LED2.cathode
  N2: Part1.D11/MOSI, Part1.+5V
  N3: Part1.A6, LED2.anode
  N4: Part1.A2, LED1.A
  N5: Part1.A1, SEN1.Signal
  VCC: Part1.3V3, U1.VCC, SEN1.Vcc

custom parts:
  Arduino Nano 33 IOT: The Arduino Nano 33 IoT is the easiest and cheapest point of entry to enhance existing devices (and creating new ones) to be part of the IoT and designing pico-network applications. Whether you are looking at building a sensor network connected to your office or home router, or if you want to create a BLE device sending data to a cellphone, the Nano 33 IoT is your one-stop-solution for many of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
  Pulse Sensor: Pulse Sensor Optical Heart Rate Monitor for Arduino and other microcontrollers
